# Fritzing sketch schematic (saved by Fritzing 0.9.3b)

parts:
  Part1 = Arduino Nano (Rev3.0)
  DS1 = DS18B20 1-Wire Temperature Sensor [part_number=DS18B20]
  DS2 = DS18B20 1-Wire Temperature Sensor [part_number=DS18B20]
  LED1 = LED - 3mm [color="Red (633nm)" package="3 mm [THT]"]
  microSD1 = MicroSD Card Module

nets:
  GND: Part1.GND, DS1.GND, DS2.GND, LED1.anode, microSD1.GND
  N1: Part1.D2, LED1.cathode
  N2: Part1.D3, DS1.DQ, DS2.DQ
  N3: Part1.D4, microSD1.CS
  N4: Part1.D11/MOSI, microSD1.MOSI
  N5: Part1.D12/MISO, microSD1.MISO
  N6: Part1.D13/SCK, microSD1.SCK
  VDD: DS1.VDD, DS2.VDD, microSD1.VCC

notes:
  SD breakout:
  VCC > 5v
  GND > GND
  CS > 4
  SCK > 13
  MOSI > 11
  MISO > 12
